# Fritzing sketch Untitled Sketch_mydogteddy (saved by Fritzing 1.0.8)
breadboards: 1

parts:
  R1 = Rotary Potentiometer (Small) [maximum_resistance=10kΩ knob_status=50% power=0.5W package=THT]
  부품1 = Arduino Uno (Rev3)
  LCD1 = LCD screen  # not connected

nets:
  N1: R1.leg1, 부품1.5V
  N2: R1.wiper, 부품1.A0
  N3: R1.leg2, 부품1.GND
